# Fritzing sketch stepper_test (saved by Fritzing 0.8.7b)
breadboards: 1

parts:
  Bauteil1 = Arduino Leonardo (Rev3b)
  M1 = Stepper Motor - Bipolar
  MD09B1 = A4988 Stepper Motor Driver Carrier
  BAT1 = BC9VPC [package=bc9vpc]
  C1 = Electrolytic Capacitor [capacitance=100µF voltage=35V package="200 mil [THT, electrolytic]"]

nets:
  5V: Bauteil1.5V, MD09B1.MS1, MD09B1.VDD
  N1: Bauteil1.GND, MD09B1.GROUND#147
  N2: Bauteil1.D12/A11, MD09B1.DIR
  N3: Bauteil1.D13_PWM, MD09B1.STEP
  N4: M1.A, MD09B1.OUT_2B
  N5: M1.C, MD09B1.OUT_2A
  N6: M1.B, MD09B1.OUT_1A
  N7: M1.D, MD09B1.OUT_1B
  N8: MD09B1.RESET, MD09B1.SLEEP
  N9: MD09B1.VMOT, BAT1.V-, C1.+
  N10: MD09B1.GROUND#141, BAT1.V+, C1.-

notes:
  Cable wiring - Stepper Motor
  A1 - Green
  A2 - Gray
  B1 - Yellow
  B2 - Red
  220 µF
  Use wiring set from data sheet
  linuxprofi.org
